# Fritzing sketch Sketch (saved by Fritzing 0.7.7b)
breadboards: 1

parts:
  Arduino1 = Arduino
  R1 = Resistor [tolerance=±5% resistance=10k package=THT]
  R2 = Photocell (LDR) [package=THT]
  LED1 = LED - 5mm [color="Red (633nm)" package="5 mm [THT]"]  # not connected

nets:
  N1: Arduino1.+5V, R2.pin_0
  N2: Arduino1.GND, R1.Pin_1
  N3: Arduino1.A0, R1.Pin_0, R2.pin_1

notes:
  Raspberry (blanc bas)
  9 53
